# Fritzing sketch Arduino Uno R3 Project (saved by Fritzing 0.9.3b)
breadboards: 1

parts:
  Part1 = Arduino Uno (Rev3)
  Part2 = HC-SR501 Body Sensor Module
  Part3 = Jtron 1 Channel Optoisolated Relay Module [package=relay]
  D1 = Schottky Diode [part_number=1N5817 package="Melf DO-213 AB [SMD]"]

nets:
  N1: Part1.D8, Part3.IN1
  N2: Part1.D4, Part2.OUT
  5V: Part1.5V, Part2.VCC, D1.anode
  GND: Part1.GND, Part2.GND, Part3.GND
  N3: Part3.VCC, D1.cathode

custom parts:
  HC-SR501 Body Sensor Module: Pyroelectric Infrared PIR Motion Sensor Detector Module

// code stored in the sketch: Arduino Uno R3 Project.ino
int irmotionPin = 4;  // Pin of IR Motion Sensor
int relayPin = 8;  // Pin of Relay Module

void setup(){
  Serial.begin(9600);
  pinMode(relayPin, OUTPUT);  // Set Pin connected to Relay as an OUTPUT
  digitalWrite(relayPin, LOW);  // Set Pin to LOW to turn Relay OFF
}

void loop(){
  
  while (digitalRead(irmotionPin) == HIGH) {  // If Motion detected 
       digitalWrite(relayPin, HIGH);  // Turn Relay ON
       Serial.println("Relay is ON");
       delay(500);
}

       digitalWrite(relayPin, LOW);  // Turn Relay OFF
       Serial.println("Relay is OFF");
       delay(500);
}
